// Logisim project Counter3Bit.circ as structural Verilog
module Counter_3bit (
);

  Clock clock_1 ();  // open: out
  LED led_1 ();  // open: in
  LED led_2 ();  // open: in
  LED led_3 ();  // open: in
  LED led_4 ();  // open: in
  LED led_5 ();  // open: in
  LED led_6 ();  // open: in
  LED led_7 ();  // open: in
endmodule
